// Logisim project Circuit.circ as structural Verilog
module eightbit2compliment (
  input  I7,
  input  I6,
  input  I5,
  input  I4,
  input  I3,
  input  I2,
  input  I1,
  input  I0,
  output O6,
  output O5,
  output O4,
  output O3,
  output O2,
  output O1,
  output O0,
  output O7
);

  wire adder_2_cout, adder_3_cout, adder_4_cout, adder_5_cout, adder_6_cout, adder_7_cout, adder_8_cout,
       not_1_out, not_2_out, not_3_out, not_4_out, not_5_out, not_6_out, not_7_out, not_8_out;

  not not_1 (not_1_out, I7);
  not not_2 (not_2_out, I6);
  Adder #(.width(1)) adder_1 (.a(not_1_out), .b(adder_2_cout), .out(O7));  // open: cin, cout
  not not_3 (not_3_out, I5);
  Adder #(.width(1)) adder_2 (.a(not_2_out), .b(adder_3_cout), .out(O6), .cout(adder_2_cout));  // open: cin
  not not_4 (not_4_out, I4);
  Adder #(.width(1)) adder_3 (.a(not_3_out), .b(adder_4_cout), .out(O5), .cout(adder_3_cout));  // open: cin
  not not_5 (not_5_out, I3);
  Adder #(.width(1)) adder_4 (.a(not_4_out), .b(adder_5_cout), .out(O4), .cout(adder_4_cout));  // open: cin
  not not_6 (not_6_out, I2);
  Adder #(.width(1)) adder_5 (.a(not_5_out), .b(adder_6_cout), .out(O3), .cout(adder_5_cout));  // open: cin
  not not_7 (not_7_out, I1);
  Adder #(.width(1)) adder_6 (.a(not_6_out), .b(adder_7_cout), .out(O2), .cout(adder_6_cout));  // open: cin
  not not_8 (not_8_out, I0);
  Adder #(.width(1)) adder_7 (.a(not_7_out), .b(adder_8_cout), .out(O1), .cout(adder_7_cout));  // open: cin
  Adder #(.width(1)) adder_8 (.a(not_8_out), .b(1'b1), .out(O0), .cout(adder_8_cout));  // open: cin
endmodule

module ControlUnit (
  input  B0,
  input  Z,
  input  Load,
  output Psel,
  output EP,
  output EA,
  output EB,
  output LA,
  output LB,
  output RstP
);

  wire not_2_out;

  not not_1 (EA, Z);
  not not_2 (not_2_out, Load);
  and and_1 (EP, not_2_out, EA);

  assign EB = EA;
  assign LA = Load;
  assign LB = Load;
  assign Psel = B0;
  assign RstP = Load;
endmodule
